// Logisim project CSA_01_Boolean_Expression_to_Circuit_and_Simplification.circ as structural Verilog: 1 circuit, main circuit main
module main (
  input  INPUT_X_UNS,
  input  INPUT_Y_UNS,
  input  INPUT_Z_UNS,
  input  INPUT_X_S,
  input  INPUT_Y_S,
  input  INPUT_Z_S
);

  wire and_1_out, and_2_out, and_3_out, and_5_out, and_6_out, and_7_out, not_1_out, not_2_out, not_3_out,
       not_4_out, not_5_out, or_1_out, or_2_out, or_3_out, or_4_out;

  not not_1 (not_1_out, INPUT_X_UNS);
  not not_2 (not_2_out, INPUT_Y_UNS);
  not not_3 (not_3_out, INPUT_Z_UNS);
  not not_4 (not_4_out, INPUT_X_S);
  not not_5 (not_5_out, INPUT_Y_S);
  and and_1 (and_1_out, not_4_out, not_5_out);
  and and_2 (and_2_out, INPUT_X_S, INPUT_Z_S);
  and and_3 (and_3_out, not_1_out, not_2_out, not_3_out);
  and and_4 (and_3_out, not_1_out, not_2_out, not_3_out);
  and and_5 (and_5_out, not_1_out, not_2_out, INPUT_Z_UNS);
  and and_6 (and_6_out, INPUT_X_UNS, not_2_out, INPUT_Z_UNS);
  and and_7 (and_7_out, INPUT_X_UNS, INPUT_Y_UNS, INPUT_Z_UNS);
  or or_1 (or_1_out, and_1_out, and_2_out);
  LED led_1 (.in(or_1_out));
  or or_2 (or_2_out, and_3_out, and_5_out);
  or or_3 (or_3_out, and_6_out, and_7_out);
  or or_4 (or_4_out, or_2_out, or_3_out);
  LED led_2 (.in(or_4_out));

  // Notes on the sheet:
  //   SIMPLIFIED SOP IMPLEMENTATION
  //   F(X,Y,Z) = Σm(0,1,5,7)
  //   F = X'Y' + XZ
  //   LAB 02 — BOOLEAN EXPRESSION TO LOGIC CIRCUIT
  //   Function:
  //   F(X,Y,Z) = Σm(0,1,5,7)
  //   Objective:
  //   Implement the unsimplified SOP form,
  //   verify it using the truth table,
  //   then compare it with the K-map simplified implementation.
  //   UNSIMPLIFIED SOP IMPLEMENTATION
  //   F(X,Y,Z) = Σm(0,1,5,7)
  //   F = X'Y'Z' + X'Y'Z + XY'Z + XYZ
  //   IMPLEMENTATION COMPARISON
  //   UNSIMPLIFIED:
  //   F = X'Y'Z' + X'Y'Z + XY'Z + XYZ
  //   SIMPLIFIED:
  //   F = X'Y' + XZ
  //   VERIFICATION:
  //   All 8 input combinations produce identical outputs.
  //   Therefore, both implementations are logically equivalent.
endmodule
