// Logisim project CSA_01_Digital_Logic_Basic_Gates.circ as structural Verilog: 1 circuit, main circuit main
module main (
  input  INPUT_A_AND,
  input  INPUT_B_AND,
  input  INPUT_A_OR,
  input  INPUT_B_OR,
  input  INPUT_A_NOT,
  input  INPUT_A_NAND,
  input  INPUT_B_NAND,
  input  INPUT_A_NOR,
  input  INPUT_B_NOR,
  input  INPUT_A_NOT_XOR,
  input  INPUT_B_XOR,
  input  INPUT_A_XOR,
  input  INPUT_B_NOT_XOR,
  input  INPUT_A_NOT_XNOR,
  input  INPUT_B_XNOR,
  input  INPUT_A_XNOR,
  input  INPUT_B_NOT_XNOR
);

  wire and_1_out, and_2_out, and_3_out, and_4_out, and_5_out, not_1_out, not_2_out, not_3_out, not_4_out,
       not_5_out, not_6_out, not_7_out, or_1_out, or_2_out, or_3_out, or_4_out, or_5_out;

  and and_1 (and_1_out, INPUT_A_NAND, INPUT_B_NAND);
  not not_1 (not_1_out, INPUT_A_NOT_XOR);
  not not_2 (not_2_out, INPUT_B_NOT_XOR);
  not not_3 (not_3_out, INPUT_A_NOT_XNOR);
  not not_4 (not_4_out, INPUT_B_NOT_XNOR);
  and and_2 (and_2_out, INPUT_A_AND, INPUT_B_AND);
  or or_1 (or_1_out, INPUT_A_OR, INPUT_B_OR);
  not not_5 (not_5_out, INPUT_A_NOT);
  or or_2 (or_2_out, INPUT_A_NOR, INPUT_B_NOR);
  and and_3 (and_3_out, not_1_out, INPUT_B_XOR);
  and and_4 (and_4_out, INPUT_A_XOR, not_2_out);
  or or_3 (or_3_out, not_3_out, INPUT_B_XNOR);
  or or_4 (or_4_out, INPUT_A_XNOR, not_4_out);
  not not_6 (not_6_out, and_1_out);
  not not_7 (not_7_out, or_2_out);
  LED OUTPUT_X_AND (.in(and_2_out));
  LED OUTPUT_X_OR (.in(or_1_out));
  LED OUTPUT_X_NOT (.in(not_5_out));
  LED OUTPUT_X_NAND (.in(not_6_out));
  LED OUTPUT_X_NOR (.in(not_7_out));
  or or_5 (or_5_out, and_3_out, and_4_out);
  LED led_1 (.in(or_5_out));
  and and_5 (and_5_out, or_3_out, or_4_out);
  LED led_2 (.in(and_5_out));
endmodule
