// Logisim project CSA_01_14_Full_Adder_Sum.circ as structural Verilog: 1 circuit, main circuit main
module main (
  input  INPUT_X,
  input  INPUT_Y,
  input  INPUT_Z,
  input  INPUT_X_XOR,
  input  INPUT_Y_XOR,
  input  INPUT_Z_XOR
);

  wire and_1_out, and_2_out, and_3_out, and_4_out, not_1_out, not_2_out, not_3_out, or_1_out, xor_1_out;

  not not_1 (not_1_out, INPUT_X);
  not not_2 (not_2_out, INPUT_Y);
  not not_3 (not_3_out, INPUT_Z);
  and and_1 (and_1_out, not_1_out, INPUT_Z);
  and and_2 (and_2_out, not_1_out, INPUT_Y, not_3_out);
  and and_3 (and_3_out, INPUT_X, not_2_out, not_3_out);
  and and_4 (and_4_out, INPUT_X, INPUT_Y, INPUT_Z);
  // Image #(.height(40), .image("data:image/png;base64,iVBORw0KGgoAAAANSUhEUgAAAH0AAAAoCAYAAADTw/VhAAADhklEQVR4Xu2ZP2vbQBiH81X0RUQ/gMkHMHQQeOiUTCUUggkEEygmQwmF4qV0MSJQ8FDQliGgJbhDSQcjD8EdAhoKGgoaDL/enXSRcjpZsi62RO4EDyR3+nP3Pu+dT6cDy7Jg0IsDscDw+jHSNcRI1xAjXUOMdA0x0jXESNcQI11DjHQNMdI1pAPSbRx/8jD/EyFeIzviCKs7D1dHtuSajnE4hOsHCKM4a/86RvQYwJ8O0RPPb5l2pQ8m8B9JoOIV5tMx3vVH8CMguLbR/3AF71cIGsbwbgJHvLYT2Bh+D0CajGhBEvTMQe86IP/4GB06GE99BLSS9M877U7ytid94CKgvpczHL/h5Vx6dp59NEvOW7gdE29jdBtS3fAve1k5l/50Xg9j2ql1CP+iG+Jbkt6HuyAm/+aDQylKZ5z7JLQxgmlfcq+WKGtTQTqlrL/tUCl9RC3QY+nWKq/F+xvQiXt+KdaVSCeM70jQwhuciPeqhMwotJ0FEVYiCPLnbcbGt9/kwocZ+mKdVDrh7Qwrcsn912aj3V0m4S4eAVzJ+ZuolE5JHkimsfO0jGU5mgknDG8jeWA2SE+eSdpwJqmrIEnQXPtTkn5tHzSeSHTtUagrk04ShT1v0SxmRXgbxPJqaknnMpLO5P8Wz6sH67w0YTZIV+gkT9LIHxXu97ysJjwBhSRilEpPk6+kblvKY1hNTelWNrrZUdLhmpRPVdVHI+myRGVTe8N+PIvFlsdLSFdpu7WNdCv7HW80OnKUZ+mORjpFCFR5G2rQ6khXmKFS6kvni55l08VPxr5/0xPywVJMoBZ/09k9pPevT03p6QqYjYx0qmy0AEpJX3f2s3rPeBppLIEV2s8F7nH1zlCc1jk1pEskK67e2XsrDRp9b33amKHIpdsXJe/E25L7LVaZHrN7kTZdO8/LpdId0l/V93T1aZ1TKZ0vusSHKb2nU/iO3IOH4aYduVMPqxfbkeMJrD5a8jty8y9OVl6Q7mDyM1Lekdu0+BUHSRWV0nfKYII5jVsc4t67wols730dY+W/1N67ZBWvhI3hjxX7PhAtfbgfS/beowAzs/eep4eTzx7uH/fwlS2d3rcdGVXYJFnpV7bon/nK1jHyi1GxTi9ev/T8RooRznj90g0FjHQNMdI1xEjXECNdQ4x0DTHSNcRI1xAjXUNalp58ABG/4Bl2i5GuIUa6hvwHfJEW8yn2VOAAAAAASUVORK5CYII="), .license("Unspecified"), .width(125)) image_1: pin names not known
  xor xor_1 (xor_1_out, INPUT_X_XOR, INPUT_Y_XOR, INPUT_Z_XOR);
  LED led_1 (.in(xor_1_out));
  or or_1 (or_1_out, and_1_out, and_2_out, and_3_out, and_4_out);
  LED led_2 (.in(or_1_out));

  // Notes on the sheet:
  //   S= x'y'z + x'yz' + xy'z' + xyz
  //   Çizelge 1.2'yi kullanarak tam toplayıcının \(S\) çıkışı için çarpımların toplamı şeklinde Boole ifade elde edin. Üç değişkenli ÖZEL-VEYA kapıları ile \(S = x \oplus y \oplus z\) şeklinde gösterin.
endmodule
