// Logisim project CSA_01_15_Majority_Circuit.circ as structural Verilog: 1 circuit, main circuit main
module main (
  input  INPUT_X,
  input  INPUT_Y,
  input  INPUT_Z
);

  wire and_1_out, and_2_out, and_3_out, or_1_out;

  and and_1 (and_1_out, INPUT_X, INPUT_Y);
  and and_2 (and_2_out, INPUT_X, INPUT_Z);
  and and_3 (and_3_out, INPUT_Y, INPUT_Z);
  or or_1 (or_1_out, and_1_out, and_2_out, and_3_out);
  LED OUTPUT_F (.in(or_1_out));

  // Notes on the sheet:
  //   Sonuç:> F = XY + XZ + YZ
  //   Üç değişkenli bir birleşik devrede giriş değişkenlerinde 1'ler 0'lardan daha fazla ise çıkış 1, diğer durumlarda çıkış 0 olsun. Doğruluk çizelgesi ve mantık şemasını çizin.
endmodule
