// Logisim project CSA_01_16_3Bit_Combinational_Circuit.circ as structural Verilog: 3 circuits, main circuit main
module main (
);

  // Image #(.height(56), .image("data:image/png;base64,iVBORw0KGgoAAAANSUhEUgAAAXQAAAA4CAYAAADtjgPwAAAO2ElEQVR4Xu2cv2sbyRfA/a8I/A8IXHyvPEEagZvAFSdIEVwF4eIwKb6INMFVECmCuCKYFAZdYdAVAbkIKE1ALgJyEVCKgFyk2MLFFi62cPFu3vzYXc3bGe3KY68VvTk+cHk7O169nXnz5s2b3dnZ2QGGYRjml4AIGIZhmM2ECBiGYZjNhAgYhmGYzYQIGIZhmM2ECBiGYZjNhAgYhmGYzYQIgAsXLly4PO5i222vQbdlDMMwzOPAY6OJwFeZYRiGqRmPjSYCX2WGYRimZjw2mgh8lRmGYZia8dhoIvBVZhiGYWrGY6OJwFeZYRiGqRmPjSYCX2WGYRimZjw2mgh8lRmGYZia8dhoIvBVZrz0YBIL5d0uYPTMvlad1ulCvovkok+ubQu9z6hQgMVZh1x7EJ4MYXGLL2EKffva1hCyX4dsa3vx2Ggi8FVmfPw1AWV+IhjfubM24OS7bAzgclsN+pEa/KjRj/UY9MaHuXqA29n2GvSQ/TpkW1sMFlumIQJfZcZD60x51PBjCK2C69U4hukNNpbA9JV9bUt4MgKl0QUMnxRcfwCOLxL5BMmXHrm2LYTs1yHb2maw2DINEfgqF9K/VO+oVElimJ/3obNL29lsMo969q5RcL0ixpOJxnBgX9sSUu/4cgCNguv3j1khCG/yuX1tWwjZr0O2td1gsWUaIvBV9tLUMV85AA478PR389Ka0H7Wge67qV5uCbv+/QTaBW1sLtqjvplCj1yrjvFkFv+0yLVtQXnHNa5QzAphq73JkP06ZFvbDRZbpiECX2UvZnmKXmWn4DpycB6pOqLM3tLrG8uh8qhDLc1PvqGG6gs17Oy0YXA+hCMifyi6MLmGegf/e7VCCDOpNuDobAz92t7nmoTs1yHbEjRejmD8NsS72Tyw2DINEfgqe+jAWNvq5OK44LrGLKNFmX8ouL6hKI861NJcezK1hRqQE5iL/06I/IHQ3nF0fkCvPRDSQbmdwSBIeBDDNzFM/rLlj5uQ/TpkW8jR5xjiz0dEvg1gsWUaIvBVdrM71BtYfs8789BrXErfA9KjDrU0l55M3fqp2aBL77jOFYpaIYTyJjfVoIfs1yHbQtigU/lOgcBX2c3bmTbUCxi5BuFuH2Y6KvNrxdDV5lmojZ4G7kXUvhlar0HHwVrrCkU6KOG8yc006CH7dci2FGzQqXynQOCr7EQOQCyu+PleDyYmJPNjBN0gy9j7ognd0znEeKAEy20Ms7870BC/YXylZ6TbBOYf2uk9zf02NEk7mt0uDL9p/Yj7Fh+PiKFqv5tBHM/gBCfD3Ra00w1lN+03E1jI1Eah06sxHGmdNl4KD//OseewBr15OIQ5xsR1ib8OoLPbhN75ArRGIfmWm+T32tDeo+0o2tD/nN2HbdnOQePlGBaxMMgFBrSc3hrQ2m+R97Q+YQ16488+TExf1L+jt9eAzt+zrN9Gk/S3KarrzduvzT0vcu9W9OHBvr62LybFJFtllWmrCkEN+m5H6cbo7mYB41dNoecBzEwmx20Ek5fL41L2JaPQ69xvT9s9EjYjhujces4lmyDsyztjS9ow/JGs3LfBYss0ROCr7CCLn8PVFIanwyXGXyOpqOR6DuO3nTUGicqS6azNU2iVnkAasqMkP8dwLI2q+jeGiJJEKPrfLjT2BzCVHbiMwWuJpWYiOl5PdGaTBmffZ3LOxYA/tO93kB7QyJVY6PcUO1hMOl51whl0aSgTYSReKwMp/y0eF/WZXOHk3obBhfo18/f0fpujT+L9fB/K1FeVBmfrrQWjK6US0t69681FQIO+L96NeNbZ+wNlINFwytOsQp/CoPb3cQNWGe74Uze97056c/EEnyXVpCriXU/PRjC7FuPlNHN6QhPOoLeFPsQYvTyBA+lEoFGVP0SoVOj5TVtuwEon4HoCXXMf9qVkDsM/G+neYF7fSJp3L5yVTK5swnJJIPoygtFX8Y5+DMlEa4PFlmmIwFe5mFz8PP4hzMA3CzFD4eCN0dgfNun9q/j/BKIbody1iWH6pqDdIvAlCS/tODcByBAIFh0GyfLuSxi8V1Px97XXl+pJeC35CUbv/mNGx7F9v4P+pdDnxUB1QOHRPz08hhPp7YqOUbACqE4og46GLIHp65yhTPWgQxppuK6EIZFH8Y3XZyZINMT5evjsWGj47/715iKUQW9J47M4yxvK7EStDGk8G4Pxr1IDc0e9ueh8jOSK+0g6P+h49WBwNoNITDDxJV0BhCSUQW8JY4yORf5Z04iDDPvlHNbUoLek0TeetKlvP4/KVsNPV+Q8bnw/YuUyeqkcnOZ+B3rvxASIfyO/wvGAxZZpiMBXuZgS8XPjleFMlA9VPDbQWC8pfydLxzQvS4ZHxCQx/7A6AwPvNZkarX+KT8mls/j3k/UNiljCjcRSLfoUyigFMujYN8RgWdoIez1Vy/54otIixYoHvblYeDGr9g2krkxsHSdLbMcOL9nt+wiuNxeBDDoaA3viT0/UiveFjoJe5sdXEzjW4zG43py0oX8RLYfP7okwBh2NNToceVlupfJBr9I/LiCOFzB5rW0D6jzNgOo5TnXnVt4r3nv7zVS8V/H+ShhzBIst0xCBr3IhK+PnkkxJpCM9aszsbL/0qqgZHctyfCw7Pbf290pwAP+MK3qYv8EAl3dkNZMhf3WBPEV4Zu737Qa9Otm2L721BL0v+hmtTJTMu1rxDZy19OamKwY90ZGlTxkWKbgmidf8AJhxqOyJ08Gd9eakDYPLOJxnfjiGha2jPBhmui2Qp1RYmS/Rh5mMpbsd1CVcE6QJ7634DpDZPyvjmRuw2DINEfgqF1Ay/3zHxO2wBPD8Hgrb+7Gvl8XZTvlZvBDcbMZY5Vm3slHCpR7dbzDg8+IX8Wx5jv01wmfE+7Gvl8Wlt5Lt30FvLhq/P6U6SunDNEYDY8tz/LHeJqy9gvRzR7252O3AEOPQF/0wxhzBkJitoxz9i1j+PVueUWXvLEfFlYpL/6tX3g3onM4huRYTeQVjjmCxZRoi8FWmpIZqVfzzIItDrZixCGJZ3Lc2WqsxgK4zY2IF+rRgWe/HRfpy7XZKzuKFYKgizu+QhyRQyIVQPU5biBl0dvhh17Tv+ZrfverNRaCQC0GfqC27gryL3lwEXumUJUzIhdL9pIPDKxxURe4jekv6X7XyxjBOBPHPLMuqClhsmYYIfJUpJeLnSMN0JKAz2Uqen8DU3mityKjkIR1Mr5t+m8LwhfJSXLNvRxjo6FP5QyfppolrF9w5izvATIebCCavbC+5IT2X+Yff6D2VCGTQ97ow/DKH6an2hF3eD64IoknpUFy6Ub2UPeBp33DvenMRyKBjet35DGbn2hN2rvxwRSBk/1u+f229uRDGfBIlMD+l2WsH/1YbI1UJY9CFl/x2DLOvY+0lu1cqhf0j3eC3x4prJaT+5tGnKM04Wrr2vNw4wGLLNETgq0xIv9+ST+exaLwYZbmaJDf2EbE70LEzY8DNZge+3Hw9nblRcpJAzG738ucOVs3iDmTaGh6L71nLdJOHHOKEZQiD3oCByQjShsLEb3ECy9eTqaIVTmUaL8oe0N448IPozUUYg56dtFbvJt1otwxxWxhuTH+zV5Vr6c0FjgOxOsB0v+6z5Rzz5ivM5Kg2RqoSxKA/zzKC5NjEbCCloeV3ZeXUp5gMNXsidK68dRo0njk57CyftcBzLj+TUuMAiy3TEIGvsmKvrWNUwgCaAxripZIY1uGx8M5yB0ce+4Eik+4lXtz4ZUMNCm3gF6dmtlYbP7iLbw8WH2bgZcu4JnT/NbqpMND1IILrBcy/R+p+szGknzX6uDr7ZjUhDHq2oSwPU8lBoZ4RM32MQZWbQslcHaoibTgwG1FpCAs9rexrnrZ39XB6cxHGoJuUWXkoSDoW+DtQkBkUPBwUYU590d+qqjcnKncbxGpn/m2R3i/1qd9xIiYH22sPSRCDbiIMclNSG1vZH3IpnTKklIjVddHfMk5fFqHAQ1/qnAqQlXcbUyRFv4u+z2GRKk31Q/X/YgIoYSOx2DINEfgqS6p9/1znn+ucS7utx0VbJfxjJ73CDBBMI9Iy+RJEx8XfU3DCbjW6HVTJT7EUFZ0gifUbteOZHqQnm/tsgjSGmbIDbvKFMOj5Dqx0hymrUib1IDr1dSIPw1TZ4VeoZasswkgvcADF+AUcLDT893B6cxHGoGP6r8zxvprLsxmYbtnUMjlZ/cR+qxwS+15FNb25kLnb19lqW00iqUIh+hJwc9RBEIMuQ0ZKF3P0jjGCsKdltzEsxOSP/bbodLfBvBNZ/wonBPFc2tFdSoGWh7BwotDvRk8UmdLKb45isWUaIvBV3gIa0PrD3iE3svw33tcjzSzZb6bpe+W/WYLPQXfuTXaF+6j8OoQx6Ih5vrzu0oyQNTM7Ctsx3hb5Ds5D6s1FGIMuMSvkfJZRumoud7y+nN7cYD8metPPcNcxUpYgBl1iTqLndZedTie/s4g0Iwf7mUl7tL4FhPohmWH671QcB1hsmYYIfJWZyuhDCTd4VDuff25O691vnHF9hEG/DWPQQ6MOduGBrfxgxhOUyi6t+g5GPWA2Slz+0w73wGbqzQ3uB9hJBg+KPhCHnwnJx89x9SJLwR5GKLDYMg0R+CozVcl/FiH1Jsz3Ye4/zvjrYSZCWIpPmjBOFS9zu2C9hSbdSM5nGOmNd+KdBwaLLdMQga8yUxWd36u+hoeybDP0IY5H/3pow4Rxd/woUn5T7zFnUNUO6y00agNVf4l1J7cZWvBVxtB4bDQR+Coza6A2BnUGgNy8WverkwySbkJhdgDOjDcRzE67pWLH2wzrLTBmQ1VnS8nEia/D9Q8xVsBjo4nAV5lZm+KNOWZ9CjfmmJWw3gJTuNl5v3hsNBH4KjMMwzA147HRROCrzDAMw9SMx0YTga8ywzAMUzMeG00EvsoMwzBMzXhsNBH4KjMMwzA147HRROCrzDAMw9SMx0YTga8ywzAMUzMeG00EsjIXLly4cHm8xbbbToPOMAzDbCREwDAMw2wmRMAwDMNsJkTAMAzDbCZEwDAMw2wmRMAwDMNsIP8Bk/iny6wd6gYAAAAASUVORK5CYII="), .license("Unspecified"), .width(372)) image_1: pin names not known
  // Image #(.height(74), .image("data:image/png;base64,iVBORw0KGgoAAAANSUhEUgAAAPoAAABKCAYAAACSJklIAAAJTElEQVR4Xu2bv2sbSRvH/a8I9A8I0hy8zQnSCNwErllIEVIdwsVhXLyYNMG8xSFSBPEWQbgw6IoDXRFQCoPSGOTiQCkMmyIgFy5UuNjCxRYunntmd0dazbOyZqXV2J77Dnwg/mpXemZnvjvP/Mje3t4eAQC8RwgAAP8QAgDAP4QAAPAPIQAA/EMIAAD/EAIAwD+EAADwDyEAAPxDCAAA/xACAMA/hAAA8A8hAAD8QwgAAP8QAgDAP4RgBQoKSjXF9NaOEIIVDgMEwFsc+kgIVjgMEABvcegjIVjhMEAAvMWhj4RghcMAAfAWhz4SghUOAwTAWxz6SAhWOAwQAG9x6CMhWOEwQAC8xaGPhGBFtQE2qXcVE92OqC0+A8BfqvXRgwjBiioDrL0fU6y+MBrRYcHnAPhKlT5agxCsqC7AQxpFyddxCaknPgfAX6rz0VqEYEVVAbb+nGqXc5lSvy6vAWVoUfdL/1+RGdWOBjT80BT6c6IqH1kgBCsqCfBlj8L7mMaX2uwRjX4ruA6UgJ/pvyQzOvwaUfT1UOjPiUp8ZIcQrNg+wBp1vsUUX/WoeTSiNHtn0783rwPlgNGfE9v7yBohWLF1gL8pc09psK//nZbwtOBaUAIY/TmxtY/sEYIV2wX4loYzotnnt+nf9T7p5H3659OfczUO+hTeZgFzif7uUlBv0PGXabp7wEVlKq38ffU29a+y1xlPV6afD6lmfG/r44SiaEK9l/I37anS6A1qn4UU3WeVuo9o8v+Aai+OaXid1ZTrEp62Cu7dM+rM937U17Wo/4OfwR/btXVlRt+4bVrU+cptnjyf/H21JLb44lj+loEqprYjhGDFNgE2T8N0K22+8KY6Z1rKN1yDWq8DCjbmFTVLLADW1DQjntHwfTNp1ORv1cwxT0OuB9Sut6h7mXaa8JO+Lz0nEH09psZ8l8E04wmN75InQKMD+bv2VGX0rLPeDOnk59r8b9WhVV2nf7Wptt+lcfLCK/q97GzEUolpdjGgwd/8vT/6yy/CDajG6Ju3zeH5fLtoXqKrIfXP2fxL/Xs1qpjajhCCFRsHWO/QhDvK5IPqPFrXD5K7wuWJvOch/jui2R13vo2JaPx7wfcWojqCWkfIxT7PRtj8b/jvD5O0IpQz+rsx/86YjpeuN3YYDrLpC193In63DBUZXU2nVCy5GGtnWd41G9Jb/rvzbV5T+XuvhzSLeWp2lL4QG/sBHX8c0IQzOeKRsaumbOY9JanE6Bu3jerH3Hc+vuUXBD+bn19R+389GnKmQmogOMr379WoYmo7QghWbBZgNip871FzSc/tpfNn8r4ngjIxj9pLsZuHfXiUm9zyCMGpuzKDuubkkkeyL+k0pflHZhYe0fLf09TbjFx/M20sRzVGVyY2p1GqHklVM3Ml6Sy/KMPTbAq2htbvY34pc2wVmFxRhdGrbJvarwOa3s1oZGlyhSqmtiOEYMVGAb7ht7yay5z3qX+WZ0hhNqKr0SIw73vCBJ/VEGWbiTR5bppWc3l+WqPe96z6n4OC+/L8RF2V+orMZEEST4E+58dgg2ccJOsqm+6M6DluqZH8YMjGKYhfo+bG9wX6nDLZ2nZtUzvivh3Zj+QaVUxtRwjBivIBqgUY7iY3PN5cSWba6M/qGGyTBtdp2OGpRQO/HGSpIY9qS/O33BzQ4hyBSoPlWoNG/QanzELPsd8Q37mWlbGvo0bBWUjx7Zg6ZUyuqDfplRl7js4lj+iXHaEvKLH+srJ+69um8U6t2/Az/9WiDxioYmo7QghWlA2wxmlvHE+os+LB67SQ7vmags9XUm9TZyk7KEuX2i8KvtcKvYjIjWyxUj5PAc30X28vlq17IdWk7oJP2XKpGfuD8FSNM57oZmi1MFWWKlJ3zaZts1GmkkMVU9sRQrCiVID19K0Ynq7eTklXdFUp2Unf9GhckCGUYfCu4HuLeNGm/kVI47N2Olcz5+caNarORukCTw5dx+i8vaTbzgHtqMboagtxfDWmfjZKmfNzTcCxz86LtpHY5Oc8Ufvep8A0+Zvi51OWKo2+Sdu0TjlTUfUwB4p6h8YRt8F/5O+YqGJqO0IIVtgHmC3AZSu18vOU+QPdentpV9Soq1eZM2MfX2RZyNIC4uo91N5VevnyoSC7OaA9FRi93qVJtneeGul4viuyFHs924UQL8qszdW+80FArbwR1B78TVz4fMpSpdHLtk1i8nuek78L6FWy/Zh9Vg+4n0RiQW8VqpjajhCCFesCVNsNwcEJDfRBBE6Jjl+3kq0Icd3rNp1cpItaarFHHcpQc6ylDvLoLBajkoMR+32a6m1iblT9tk9SuTgsPPSiV3UXC3cNav+lD9msngOWowKjq62xJNBpsrjUOtOHQniScqY7dSvp0MkRZuP+1AQxzb6HNNWJmjpncJc9sAemcGWo0uhl2iY5O8HPI7rmJz3TdcrVT2+1FvyOiSqmtiOEYMXDAf40X8FcLuZcdtV1aTG3dx6bRQeespnTE2GJRuki4/SWG/vB+VprfogkvpkmC5BxlDlh6/1zTQVG13HezSi8Viv8akss03L1VycCxaEX9R+V4mixxcSjvhrB52W2waLcCqo0un3bpFnM4jRg+sKbl5KLcqqY2o4QghUOA3xSpBnIcrqmteCX9HCIeY/JfNV8vzHfnqNvXat711OF0RU1av5irlxrzUhX87xoFazqZ6cXLZ+PLdUaPWVt26idAFEP/VxkxroOhz4SghUOA/QAtfo8TQ6XTD7lsxR9UKhonrspbPT7Koz+9GmfR2LxrDwu20bi0EdCsMJhgM+f3H/aWYxA+uw4d6VvnUpHOlCCR24bVUxtRwjBCocBPn/q6X57fD3MtmIWCz3if7kBtzxy2zj0kRCscBigF6QLebQ4unkb0vBDsNPRAtjxmG3j0EdCsMJhgB6hFm1KHMsEDnmctnHoIyFY4TBAALzFoY+EYIXDAAHwFoc+EoIVDgMEwFsc+kgIVjgMEABvcegjIVjhMEAAvMWhj4RghcMAAfAWhz4SghUOAwTAWxz6SAhWoKCgVFNMb+0IIQAA/EMIAAD/EAIAwD+EAADwDyEAAPxDCAAA/xACAMA/hAAA8A8hAAD8QwgAAP8QAgDAP4QAAPAPIQAA/EMIAAD/EAIAwD+EAADwDyEAAPxDCAAA/xACAMAz/gFe/RwOI90zCwAAAABJRU5ErkJggg=="), .license("Unspecified"), .width(250)) image_2: pin names not known
  // Image #(.height(54), .image("data:image/png;base64,iVBORw0KGgoAAAANSUhEUgAAAHcAAAA2CAYAAAD9PQZDAAAEuklEQVR4Xu2aP2vjSBjG81UE/gKGba5cwzYCN9utIcUSrljCFodJZdIsLs0Vi6tFXBHQFQZfEfAVC94m4O3kwuAUC7oihYoUKlKoSPHsjCWdE71vopHsYePRTPg1z1jOo+eVNH/ko6OjI1iMhQgWcyCCxRyIYDEHIljMgQgWcyCCxRyIYDEHIrDYprcV894TRGDRaKDxaMyWCCwaDTQejdkSgUWjgcajMVsisGg00Hg0ZksEFo0GGo/GbInAotFA49GYLRFYNBpoPBqzJQKLRgOGMsA8FqHdh5geF/seozFbIrBoNGAmf8whawtEmNnimkVnEm4yww8fHab/IRqzJQLL7gYcdH4fwpvMEazWWAuCbz6G79vbz7T6mH710CPHHhoOvOu0tsFnh+l/zO7ZPgkRWOobaOP0ywLhXXqySGJE12lx19cREvEXXfbhiMLOI9G/HDHfcWgMsZDne7fAgPRR6mdbChFYahnojjC/SdKixmv4Zx04hc8473yskwRxnH4unHTo9xwaH9PxNrka0D6GWtmqQQSWqgacD1OEeV2/j+Ayn8np/J2NTyKS+Ufaf2ik462YSL2nfRxVs60AEVgqGeh64m7MyvWtT+5WQsvHprziMTYs9h0g3gpKE6mcStlWgwgs6gbE2HmbFha3c/RJP0c/XRMaMd6m56IykcpRz7YyRGBRNXByKWdFsiVYfFI9wTQQI8ZbQbvros3oT6GabQ2IwKJkoDVGcJ/VNprhpNj/JANMVwt4JYv9X43zQUz+8qdSHGDczfq6YlhJQvhv6DEqKGVbDyKwqBjYToxEbS97pH+fOK/fonfcq0/3wfpahTfbecT/LYmwmEwR3CYIL1x6jCKyFbU9QQQWFQObicSm6Z71/ib+l1gh3+3Aj2mlzZKeGG7kMf3Xcqhpwz0eYDwJEIknVbwcP7saKEMl25oQgaXcQDYpku0+wIj0m4aL0XdR8JW3U2El5dnWhggs5QYG6a6MbGKWfEr6n8LF4Muwwvj8EnAxXsY737E55dnWhggs5QYe3LlijVe6ts2Rb08Ut+leBK0e/OukdGOmCuXZ1oYILOUGOpj+lxU3Vl3fOhgt5d7yCdP3PO65B//Cr433qad+Aea0+pjdxOleeLFvB8qzrQ0RWFQMbGfLIaYKywLnzwCJvBBatO95HAwvs5cPdbmq+PZp82IjwfqCXhQn/4SIvqrtI3OoZFsTIrAoGWhlb0NQvu3onInHsVhKzM5UNzp+IbKwt3JW7OH0+PEGRft8hihJsDhnjlNEKdt6EIFF1YAsmlweyBZdjdAr3pVizBr+G4rlSHgYhRWTJ0+MsbiLxB0fZr+uQLqcyta9yXL07IVchmq2NSACSxUDzrsxgjwF0eKb7FEoxqtErgtXPk5f0eNeIp2/1kjkHnl2kTpn8k7dnpu8gHedWMlW1PYEEViqGyj88uJqBv/zAO6BFDWn3e1Rz6/czS7X282GBj2mKtWzVYYILBoNNB6N2RKBRaOBxqMxWyKwaDTQeDRmSwQWjQYaj8ZsicCi0UDj0ZgtEVg0Gmg8GrMlAottelsx7z1BBIs5EMFiDkSwmAMRLOZABIs5EMFiDkSwmAMRLOZABIsh/ARMaFOrxNOgrQAAAABJRU5ErkJggg=="), .license("Unspecified"), .width(119)) image_3: pin names not known

  // Notes on the sheet:
  //   Giriş değişkenleri \(x,y,z\) ve çıkış değişkenleri \(A,B,C\) olan bir birleşik devre tasarlansın. 
  //   İkili giriş 0, 1, 2, 3 olduğunda çıkış girişten bir fazla, diğer durumda bir az olsun. Doğruluk çizelgesi ve mantık şemasını çizin.
endmodule

module Generated_Implementation (
  input  X,
  input  Y,
  input  Z,
  output A,
  output B,
  output C
);

  wire and_1_out, and_2_out, and_3_out, and_4_out, and_5_out, and_6_out, and_7_out, not_1_out, not_2_out;

  // Image #(.height(53), .image("data:image/png;base64,iVBORw0KGgoAAAANSUhEUgAAAWsAAAA1CAYAAACHtcpLAAAN3klEQVR4Xu2cv2sbyRfA/a8s+B8QpPheeYI0AjeBK06QIrgKwsVhUnwRaYKrIFIEcUUwKQy6wqArAnIRUJqAXATkwqAUAblIsYWLLVxs4eLdvPmxu5q3Y+2uRtI6ent84PLWO5Lezrx5896b2dvb2wOGYRim9hABwzAMUz+IgGEYhqkfRMAwDMPUDyJgGIZh6gcRMAzDMPWDCBiGYZj6QQQMwzBM/SAChmEYpn4QAeOkC+MIAO7nMHxu3ytP82wOeMWXPXJvV+h+QYUCzM/b5N5GeDqA+T2+hAn07Hs7g89+7bMtxoIIGBd/jUGZlhBGK3fEAE6/y8YArnbVWB+rgY0a/bQdYx18nKkvcD/dXWPts1/7bIuxIQLGQfNcecLwYwDNnPvlOIHJHTYWw+S1fW9HeDoEpdE5DJ7m3N8AJ5ex/Abx1y65tyv47Nc+22IIRMDkknrC0/dBzv2SGA8kHMGhfW9HSLzaqz4EOffXj/HshRf4wr63K/js1z7bYnIgAkLvSr2AQlccweyiB+192s7jRnvCdxPoknvlMR7I/J8mubcrKK92iysL49nvtBfos1/7bIvJgQicNHRCTHoiR2149ruZPRvQet6GzvuJjleJIfj9FFo5bTxajpQn7Gu5fHqNWtre8n/7dGB8u+WB/UF59rs8YXrt1z7bYvIgAicmvodL93bOfeTwIlR/I67pO3r/saI8YV/LZe2BbG35j7SgfzGAYyLfENqrDS8O6b0NIfvz/RT6XlaBARyfj6D3yCZfn/3aZ1tI8GoIo3c7PJFSiMBBG0baDseXJzn3NSYOKa7Zx5z7jxTpCftaLksPZIvLf8kpzMR/p0S+IaRXu82VhfLs/XmBGP+OYPyXLa83Pvu1z7aQ4y8RRF+OiXyHIYJ89gc6c/+wx5x61ts2Rj5RiShfSZMAw0lbTyxu11jjQNzqykL2Z39e4OM01j77tc+2FGysCUSQz7upNsJzGLq8of0eTHWk5FeLWTcOWtDIkVdivwmtJN6/LbZrrPeetKD1JEe+MQJoHjQ9ThaP0Vj77dc+20LYWBOIIBfpCeHlilc/6cLYhEl+DKHjJQ64LhrQOZtBhDvX8LqPYPp3GwLxG0Y3era5j2H2sZXzbA77HRhca/2I5+afjokRaL2fQhRN4dQ10eXQejuGuazFFjq9GcGx1mnwagzRyok5v8a6cTSAGSYM9RV960N7vwHdizlojUJ8XXQCb0HvS/octmU/F7wawTwSnnGOcVyv3lz4NdbBnz0Ym76of0f3SQDtv6dpvw3HyW9TrKY3F8HLzLsVfbh/oO8diNVJvL5Qlldjvd9WujG6u5vD6HVD6LkPU1MVcR/C+NWiEyX7klHobea3J+0eC5sRQXhhfc8FmyDsy3tjS1ow+BFXTWoTQQ5pvBpuJjA4Gyww+hZKJcS3Mxi9axNDtRxVTdKuzDNoFp4cAtkJ4p8jOJHerfo3hm3iWCjx3w4EB32YyM5ZxJg14fQ6Fp2qK7wKU7drP2c2wIjBfGQ/7yDZCZa5IqHfM+w8EelU5fFnrKURjIUBeKM8Vflv8XVRn/ENTtwt6F+qXzP7QJ+3Of4s3s/3gSz/VHW7tt6aMLxRKiHtrV1vLjwa6wPxbsR3nX44VJ4qGkW5JV7oUxjL3gEmM5VRjj53kudW0puLp/hdEk2qS7zryfkQprdivJwVdGgq4M9Yt4Q+xBi9OoVDuZpDgyl/iFCp0PPblkxmygn+dgwd8xz2pXgGgz+DJBeX1TeSbAISjkgqVzZh8Yoh/DqE4Tfxjn4MyCRaECKgZOLV0Q8xxK8txMyCAzNCQ37UoM8v4/9jCO+E4ioTweRtTrt54AsQ3tVJxrjLGDJeOo6c1pUXMGavJ+LztbeW6El4G9nJQ5c0YZnaif28g96V0OdlX3Wu/SY8OzqBU+mlipee47mXx5exRiMVw+RNxggmetAx4SSEVsBIyLM6jLdmJj80stm/w++OFw3JrV9vLnwZ66Y0LPPzrBFMt+XLmPDzERjfKTEeK+rNRftTKFfKx9KxQaeqC/3zKYRi8oiuqOfuE1/GuikMLToN2e+aRApk3iTjjCbGuikNuvGAzd/b30eV4OLZNhlPGd+PWHEMXynnpXHQhu57MbnhZ2RXJuUhAkqBeLXxpnAGKRw+2AJoiBcUu5eWJJoXIUMWYgKYfVxeVobPmvKz5j/5W22T2ff7aXVjIZZVQ7F8Cj/7MjiejDX2DTEQFioA3kzUUjwaq9JAsVJBLywS3seypKrUlUk84kSI7dihC7v9h/CuNxeejDUOdHtST7bli/eFToBeekc3YzjR49G73py0oHcZlghpVcePsUZDjM5EVpZZYXzUq+tPc4iiOYzfaNuAOk/KOruOoyEyK+Yl7731diLeq3h/1Q01QgSEpfFqSaoA0klqjZlV7RdaFjUT47UYj0q34FY+rAgH58+opGf4G/RxyUVWISnyV+fIE4RH5X7fbtAbk20/VOJZgO5X/R2t8rrUK1pyAFYlvbnpiAFNdGTpU4Yqcu5Jooon+xlnyZ4UHaysNyct6F9F/jzqoxHMbR1lwdDPfY48ocSKeoEeTGXs2u18LuCa/EzIbckhYCZftYJHbSACi4L11XsmToaXB49tU9hei32/KM52is++uWDiFmOD553SBgeXXzS+b8Dvi8dY2vIMBxVCWsRrse8XxaW3gu2voDcXwe/PqI4SejCJ0HjY8gx/VKs+sVd+D7Oi3lzst2GAcd/Lnh9DjWCYytZRht5lJD/PlqeUyVVlKLnCcOl/+Yo5gPbZDOJbMUmvbqgRIlgkMULL4o2HadxnyUxDEEvVnpW0LEcfOlXLwPSW46Jei4vkxdntFJx9c8HwQZTNJPvEUxiEUD4umosZUHZIYN+0/8ARnGvVmwtPYRCC3pZfdOW3it5ceF6hFMVPGITS+awDtkucT0XmdMwF/S9bMWNoJYToZ1qN5AEiWKRAvBoJTCcBOgMt5cUpTOykZUmGBTfgYInZ5HoCg5fKu3DNmm1hfMPPxXe3JQkIV7bYOfs6wIqAuxDGr23vNpAex+zjb/SZUngy1k86MPg6g8mZ9mBdXgt68uG4cHgsSfouZNkfaN+wdr258GSsscTsYgrTC+3BOlds6MkL2f8Wn6+sNxfCUI/DGGZntMrr8N9yY6Qsfoy18G7fjWD6baS9W/cKI7d/JMlye6y4VjDqM48/h0llzsK9F+XGgQURLJCcB5ItabEIXg7TWkRS+1kj9vs6VmWMs0kc4IvL/p2ucCg4ASAmK7y4xX7Z7OtAlm7huRlda+ls6mx91Lb6MNYB9E3ljDYCJl6Kk1P272S5ZImt3cb7sQfrg3HXjejNhR9jne4AVu8mSVpbRrYljDKWgNmrwUp6c4HjQHj1WPLWeb644aXxGiseyo2Rsngx1i/Syhk5NrFqRmlo8V25asZNJZc9yTlXzLoUGPdUHLUXN37hPo6fcalxYEEEcneZigkJ42Y2F4gXRmJGRyfCq8pseqj7ZhhT8iReyuhVoDq8Nt7zMzPLqiQKZrvtgfAQZlClS6sGdP41uikxiPUAgds5zL6H6nmTZNHfNfy0vEplOT6MdZqclRuBZIdX3xErYoyxlAmWeFZqQ1CS1EnCSughpac62l7R5vTmwo+xNmWjckOLdBrwd6AgNRa4sSXEmvG8zyqrNyeqNhnEKmV2PU+el/rU7zgWht/2tn3ixVibyIBM8GlDKvtDpqxRhnlisSrO+yzj0KWRBdywpPZhAFkxt7BMUPS78PsM5onSVD9U/y+Me3UbSQQlz6/W9dW6ptBuq160VLE6dsAbrJTAUhotkwoWnRJ/T87Or+XodlAlP8XyULzgONJvy44fPoD0QDNb9aWhS5XtMWHmw1hnO6fSHZZtSpnUg+iwt7HcyFE+E66WkvISBniOgyPC46/woiG5zenNhR9jjSWwsob5Zib3HmDJYUPL5ET0E/utcjbsZxXl9OZC1ibfpqtkNUEkCoXwq8dEowMvxlqGcZQuZujV4sr/iZbdRzAXEzv227xdxwbzTuTf36CxF99LO7ELZcByAxFOAvrd6EkgVdrKiUYi+MUJoPmHnUk2suwZ3dVIKjAOGkkJW/EDi/B70Ay3qULwe5aGH2ONmO+X1V1SOVGxAiK3HeMlkUOwNqk3F36MtcSsbLPVOMlqt9j5G8X05gb7MdGb/g6rjpGieDHWErNDOqu7dNc0+Z15JJUr2M9M6Z91EBjqh1RQ6c9ZcRxoiIAphS6ov8Ptwdn6arOLbL1xveoIY33vx1j7Rm1Kws1G2YGKO/uUzal4rsKawaqNqPhxAmvgcerNDcbf7YT9RtGbufBoimy8Glcd8srJGawZImDKkN2Kn3gB5ryR9cf1fj3MJAcL8UATWinjHe4WrDffJEnZbCWOTmITr3ozEAFTBl2/qk5FQ1maWNzEltxfD210MM6NB+hkE2R1rjTaOqw336hkpD6Rcy+TWMw5nW9DEAFTEpVk05lymQiqevoggyQJHcyi46x3F8L0rFMoVrvLsN48Y5KTuqpIFiF8G1TfgLc6RMBUIj/JxVQnN8nFLIX15pncxOFWIAKGYRimfhABwzAMUz+IgGEYhqkfRMAwDMPUDyJgGIZh6gcRMAzDMPWDCBiGYZj6QQQMwzBM/SAChmEYpn4QAcMwDFM/iIBhGIapH0TAMAzD1A8iYBiGYeoHETAMwzD1gwgYhmGY+kEEDMMwTP0gAoZhGKZm/AcxswuVJoYGIQAAAABJRU5ErkJggg=="), .license("Unspecified"), .width(363)) image_1: pin names not known
  // Image #(.height(42), .image("data:image/png;base64,iVBORw0KGgoAAAANSUhEUgAAAOEAAAAqCAYAAABFnDwNAAAHnklEQVR4Xu2bvWvjShDA868I/A8Y0hy85gzXCNIErhGkCKkOk+IIKR4mzRFecZgUwbziMCkCvuLAVwR8RcBpAk5x4BQBpThQihQqUqhIoSLF3KxWK0saOdbKe7p8jOAH8ehrd2dndz6UlZWVFWAY5q9CBAzD1AsRMAxTL0TAMEy9EAHDMPVCBAzD1AsRMAxTL0TAMEy9EIFhWtC/CgHuxtAm5xiGWSkQGMX6NAE0QYBgDDsF5xmGoQKD7MA4EBYoDhf65DzDMCsFAmPY3zxlgXh4MGjQaxgdbOj9GLwKj8LaHcLooEXkLxQiMMO7PrgPIUwulCEGMP5YcB2jAY7pK/Eods4CCM52iPyFQgQGsKB7GUJ41YfW7hikR4oG+Sl/HaMHG+ELhQiW56MwPA+Ga+pvebhHBdcyGrARvlCIYEm2YOQD+Cdb8ndjAMoh9b49fR+/uT0A9y5uMB7Bzx44jSZ0fngyy4uH2OHt9H2NNgyu4qUGXXDvZAes3HPtwykEwRT67+g7y2PSCJvQPnYheIg79RDA9H8HrNUOjG7inmJf3CO74N6VXJ/x3kN1nQ2DXzgGX5fTtTEjrKwbG7pnqPNofNL3WVHbwvMOfVd1iGApWkeuLEckSRgxceShP6hNsDcccCqzDi2NZJAlXOfQh9GnVjTg0W+hghBd65shtBs29C6kQt0v6j5ZBw3OOtBMssF5Q9mHyX00AjDepu8tjykjjCfS7Qj231rJbzHZRF+9722w1nowiRajovfFtd/MEYJ/PoThT3zur0F2kaqAGSOsrpud0yStnxzB1QgGp2iYmfltBCKoTqMLU1Ti9EAoVslVJ1FNF/v0nsf4dwz+PU6MygQw+Vzw3EKEkkTcmmp7soujYW7i74NpopDECPcm+J4JdDLX5zLB27FLjtftk/fqYMgIRYgg2pJqo3Uc+yv+CLbwd/cy6Sl938YI/BDDjV25WDXXHOgcDmGKHhDgjtITYUj+Hk2MGGFl3Yh5jHPncAuNF8fm7Tq0/+vDCHd4EIv0bnp+G4EIKhKvptd9aGXkqVohnqP3PRGEgeFul2l7/kMD3B2md7iyojsqJqq4Zv8Cd4Af0vVufY0nMu4E6ee0VKkG+593hfQwY4TCwPKhgehH1NV44kcuGi5i7lEcVizA/jzBBRPbZsAABSaM0KRurA9D8O59GJs3QAERVGMTV0fhO58OYHCcZgRuvBOKVdbJ3/eEcU7E0l52B29hLCS7mY2HLOhfx90/cQruS/MGesKdIzv6jKg9BfKEX8MKY+xEcXzVDLaKqbR2wO0RTuqC9itELPZQIE/Q8XKW0421i3M7+CM7oIIIKiCCcVThLa7TVxRfGeGz+nStBcMb2Wz3qMTgvxvG7g7uBpl4IRVzlKiTCteOxrYK8Q50A4k8xVqTPHMhc9u+CAucYxfCuwl0dQxQ0GjBer7tKboYewcXXSKfoRHvz+3fYt0090SeAMf8Q4k5UB0i0MZCVy4Mp9CdMyjK1YEHvKbg/FwabehmdlVdetBeLXhuKVRCCRVQIqOZuDV5l1aVaHT7XogZd5TwJU6d5dv+KBh+oKcQ3I5MJykiTLijiqq6qbTDV4MI9GjI1cQ9mp+Slpk3cWhOoM0+TAp2Vh2GewXPLWK1DYNzFybHbRkb5ONBhdiN/LEM9lOoPgan7Yy8bMxRDjNGKMowk6sJDOLVPR8PKhxsu39alIpHAzzF4ON6AE7eADeLx0cXk0ZYRTf2Ee7woh/5RbzRhUmAOviHvmcJiECDOBkTZ9ToeUnS2aVT9H8KC3oqGxgbXec83r0zyaT5NaL+lbw8+0FCuZijPAaMsNGDaVwblJO8k2SvM21vxNlisojFOhd1tW0H7PQkFTXG27BwfHQxaYS6uokM8AFjwD0H1qMSTnyu4eA8CUhyxwBEsBCRsnW292GoiqC4zXc27CidS67baMP+uUxwiMBfFISFT59R3l9nlpiIirJrA/BUGQwHXK2SkXsSuoUFd5V9myVxmtD+rgr882MOPQwYoSgvRA31okSDfawK0uh4H6sJZ0eTLfrsMHe/nKAh+NcueMrBEXXU+3jAHglLdDBphDq6iWrDOB7BDY60r/qU6p8qVxW8ZwmIYAFvkkxT9sjHTvOuk0c+Rf63mU0uDw1NfikSyUAmnLw7VMSj8YGdFLDDWy9KRoVBPEuXrg8qDBihaue9D+6NyMSKskIsS/VffClECu7io/wwmKXpcbcUO19y+BUSNHMwaYTldSN3/9lXQnIxSo4/l6AhgleL3LmzLoiSOe9lYTp/T54ku7nWTEoccNkrde9iTBihwILW+3yGUclyLliaVbsg+xp/1VRyfMpi1gglC3UjMrakH2pcqKdnECJgtBBZQi8qbE+/pHd39ZFCUVxVFTTCBxNG+PRpnwYkkaJPnbpZCiJgdEh9oD5budW3mKjmy67RHYLR4PnohggYHRqynhjejOJ09izoJ/9twdTL89ENETCayKQOzD63unNhdOA8lVX2VfNMdEMETCVEAK/xKRVTI09eN0TAMEy9EAHDMPVCBAzD1AsRMAxTL0TAMEy9EAHDMPVCBAzD1AsRMAxTL0TAMEy9EAHDMDXyGxkFEtdz+zTqAAAAAElFTkSuQmCC"), .license("Unspecified"), .width(225)) image_2: pin names not known
  // Image #(.height(42), .image("data:image/png;base64,iVBORw0KGgoAAAANSUhEUgAAAGoAAAAqCAYAAABbec77AAADuklEQVR4Xu2Zv2siQRTH/VcW/AeENFdGSLNgky4LFkGuCJLiECtJEyzlimAVlisCe4XgFYJXBEwjmG4tBC0Ce0WKLSy2SDFFiu/NuLtnzjeuP+7czIYZ+RR+347u+mbevPfM5XI5aDIBETRqQgSNmhBBoyZE0KgJETRqQgSNmhBBs5EGBgGAVw/d8qrtYBBBs4kvAwg/AT762XKUgeLnJuzOAO5kiinHfXDQPC8sr8nX0L23YZG52aPY8RZuwpODosR+IIiwAwVUb0fwXsL7Bgvgz0JHTWc+GH/5vRoM7qSBz+3jluQzsoYBexY+rntjSOwHgwjbUWph8MzCOw6mcOpFGCvXGGcOpowhCMLrvE6Rfk7maGIkFubLCA1iOyhE2Ihx0YUX++ixBVNyTUzxexQmeFQfXFJ75rgMzyc2bFDbYSFCMiWb75Lop3+okV1EyDtYuIqvwOaqLYOE5xNPIs6p7cAQIQF+1syjDTIfoEbsMmphKvshzqcc7AnSTiJiiLCWSk9kBGIwjK63PUhDR32M8yl8lpSTiBgiyMm34b5GfvL7qKza19JAdzKCnV69sRfGBU984mgRuGiXIluJh27mwTkJ3xdKJgqS+SlABCnLpID7qWcR+//EOD6FVbb2p/SmftuGk+W5+2cwH6NOF+6cwbsz6Zz0IYKURWxejENnb5/4d/EK7OUfeOruVFhbPKSLObVjEdIKMMsNtDsufB5BgnE7MatNESJIiBICMV5dtIj9o2Gi9cidN7FVcZKACBIaYZEnBs/2qsS+DhON2+YO55kKmGiPA5V2UgwRJLzZUTw13Vg7xYjmZfoV/P7kLTgztrGIfyeIIKGI7q/IUcG29ZOB1lj0+ioSWzLmlQ3nztkb+9rafjHF5GvoPwdhb3LVpgZEkLLM+jx0o1Q1CeOrCyacmqe2ZAw0e1Fjd1+GO3bpF01jhukddXDlhwf/PvV2kQwiyMlHzUixqTa0jow6D3k8ve3X36Uw3A3hpLnI7mxUy3/XSIWrPnzGi/srybz0IcJahANEyiqGP2zBWt0tPMY3f3o8Rfay4SSeONj8TMKLz3eiF/0ZiDDFj+oqNm4lLsoUIUIixlkbbvxEfATPUbjh8Z2JumPioHpE56lI8dsUTPQsowVn1MUOWj6bWIwKJRVE2IKVf3SHfTg3DZgZcVBMoWTRez4yF92N00XxS+e8I0TQqAkRNGpCBI2aEEGjJkTQqAkRNGpCBI2aEEGjJkTQqAkRNGpCBI2aEEGjJkTQqAkRNAryG7+HxZ4PBR27AAAAAElFTkSuQmCC"), .license("Unspecified"), .width(106)) image_3: pin names not known
  not not_1 (not_1_out, X);
  not not_2 (not_2_out, Y);
  not not_3 (C, Z);
  and and_1 (and_1_out, Y, Z);
  and and_2 (and_2_out, X, Z);
  and and_3 (and_3_out, X, Y);
  and and_4 (and_4_out, not_1_out, not_2_out, Z);
  and and_5 (and_5_out, not_1_out, Y, C);
  and and_6 (and_6_out, X, not_2_out, C);
  and and_7 (and_7_out, X, Y, Z);
  or or_1 (A, and_1_out, and_2_out, and_3_out);
  or or_2 (B, and_4_out, and_5_out, and_6_out, and_7_out);

  // Notes on the sheet:
  //   Giriş değişkenleri \(x,y,z\) ve çıkış değişkenleri \(A,B,C\) olan bir birleşik devre tasarlansın. 
  //   İkili giriş 0, 1, 2, 3 olduğunda çıkış girişten bir fazla, diğer durumda bir az olsun. Doğruluk çizelgesi ve mantık şemasını çizin.
endmodule

module Generated_3Bit_Combinational_Circuit (
  input  X,
  input  Y,
  input  Z,
  output A,
  output B,
  output C
);

  wire and_1_out, and_2_out, and_3_out, and_4_out, and_5_out, and_6_out, and_7_out, not_1_out, not_2_out;

  not not_1 (not_1_out, X);
  not not_2 (not_2_out, Y);
  not not_3 (C, Z);
  and and_1 (and_1_out, Y, Z);
  and and_2 (and_2_out, X, Z);
  or or_1 (A, and_1_out, and_2_out, and_3_out);
  and and_3 (and_3_out, X, Y);
  and and_4 (and_4_out, not_1_out, not_2_out, Z);
  and and_5 (and_5_out, not_1_out, Y, C);
  and and_6 (and_6_out, X, not_2_out, C);
  and and_7 (and_7_out, X, Y, Z);
  or or_2 (B, and_4_out, and_5_out, and_6_out, and_7_out);
endmodule
