// Logisim project CSA_01_17_JK_to_D_Flip_Flop.circ as structural Verilog: 1 circuit, main circuit main
module main (
  input  INPUT_D,
  input  INPUT_CLOCK
);

  wire not_1_out;

  not not_1 (not_1_out, INPUT_D);
  J_K_Flip_Flop j_k_ff_1 (.J(INPUT_D), .K(not_1_out), .clk(INPUT_CLOCK));  // open: Q, Qn, preset, reset

  // Notes on the sheet:
  //   JK yaz-bozun girişleri arasına 1 tersleyen ekleyerek D yaz-bozunun elde edilmesini gösterin.
endmodule
